# Fritzing sketch cleaningRobot (saved by Fritzing 0.9.10b)
breadboards: 1

parts:
  Part1 = Arduino Mega ADK (Rev3)
  R1 = Resistor [tolerance=±5% resistance=220 package="0402 [SMD]"]
  R2 = Resistor [tolerance=±10% resistance=100 package="0402 [SMD]"]
  LED1 = smd LED [color="Red (633nm)" package="1206 [SMD]"]
  R3 = Resistor [tolerance=±10% resistance=100 package="0402 [SMD]"]
  part = smd LED [color="Red (633nm)" package="1206 [SMD]"]
  LED3 = smd LED [color="Red (633nm)" package="1206 [SMD]"]
  R4 = Resistor [tolerance=±10% resistance=100 package="0402 [SMD]"]
  LED4 = smd LED [color="Red (633nm)" package="1206 [SMD]"]
  R5 = Resistor [tolerance=±10% resistance=100 package="0402 [SMD]"]
  LED5 = smd LED [color="Red (633nm)" package="1206 [SMD]"]
  LED6 = smd LED [color="Red (633nm)" package="1206 [SMD]"]
  R7 = Resistor [tolerance=±5% resistance=220 package="0402 [SMD]"]
  LED8 = smd LED [color="Red (633nm)" package="1206 [SMD]"]
  R8 = Resistor [tolerance=±5% resistance=220 package="0402 [SMD]"]
  LED9 = smd LED [color="Red (633nm)" package="1206 [SMD]"]
  R9 = Resistor [tolerance=±5% resistance=220 package="0402 [SMD]"]
  LED10 = smd LED [color="Red (633nm)" package="1206 [SMD]"]  # not connected
  R10 = Resistor [tolerance=±5% resistance=220 package="0402 [SMD]"]
  LED11 = smd LED [color="Red (633nm)" package="1206 [SMD]"]
  IC1 = L293D [package=THT]
  M1 = DC Motor [voltage_(max)=6V voltage_(min)=3V]
  U1 = LIPO-2000mAh [package=lipo-2000]
  M2 = DC Motor [voltage_(max)=6V voltage_(min)=3V]
  U2 = LIPO-2000mAh [package=lipo-2000]
  M3 = DC Motor [voltage_(max)=6V voltage_(min)=3V]
  IC2 = L293D [package=THT]
  M4 = linear actuator [package=THT]
  IC3 = L293D [package=THT]
  U3 = LIPO-2000mAh [package=lipo-2000]
  M5 = DC Motor [voltage_(max)=6V voltage_(min)=3V]
  R6 = Resistor [tolerance=±10% resistance=100 package="0402 [SMD]"]

nets:
  N1: Part1.D13_PWM, IC1.Enable_1
  N2: Part1.D11_PWM, IC1.In_4
  N3: Part1.D10_PWM, IC1.In_3
  N4: Part1.D9_PWM, IC1.Enable_2
  N5: Part1.D8_PWM, IC1.In_2
  N6: Part1.D2_PWM, IC3.Enable_1
  N7: Part1.D5_PWM, IC2.Enable_2
  N8: Part1.D6_PWM, IC2.Enable_1
  N9: Part1.5V, IC1.+V, IC2.+V
  N10: Part1.D22, R1.Pin_0
  N11: Part1.D23, IC1.In_1
  N12: Part1.D24, IC2.In_1
  N13: Part1.D25, R2.Pin_0
  N14: Part1.D26, IC2.In_2
  N15: Part1.D27, IC2.In_4
  N16: Part1.D28, R3.Pin_0
  N17: Part1.D29, IC2.In_3
  N18: Part1.D31, R4.Pin_0
  N19: Part1.D34, R5.Pin_0
  N20: Part1.D35, IC3.In_1
  N21: Part1.D36, IC3.In_2
  N22: Part1.D37, R6.Pin_0
  N23: Part1.D38, R7.Pin_0
  N24: Part1.D41, R8.Pin_0
  N25: Part1.D44, R9.Pin_0
  N26: Part1.D47, R10.Pin_0
  N27: R1.Pin_1, LED1.anode
  N28: R2.Pin_1, part.anode
  GND: LED1.cathode, part.cathode, LED3.cathode, LED4.cathode, LED5.cathode, LED6.cathode, LED8.cathode, LED9.cathode, R9.Pin_1, LED11.cathode, IC1.0V, U1.-, U2.-, IC2.0V, IC3.0V, U3.-
  N29: R3.Pin_1, LED3.anode
  N30: R4.Pin_1, LED4.anode
  N31: R5.Pin_1, LED5.anode
  N32: LED6.anode, R6.Pin_1
  N33: R7.Pin_1, LED8.anode
  N34: R8.Pin_1, LED9.anode
  N35: R10.Pin_1, LED11.anode
  N36: IC1.Out_1_(_Controlled_by_Enable_1_), M1.pin_1
  N37: IC1.Out_2_(_Controlled_by_Enable_1_), M1.pin_2
  N38: IC1.+Vmotor, U1.+
  N39: IC1.Out_3_(_Controlled_by_Enable_2_), M2.pin_2
  N40: IC1.Out_4_(_Controlled_by_Enable_2_), M2.pin_1
  N41: U2.+, IC2.+Vmotor
  N42: M3.pin_1, IC2.Out_1_(_Controlled_by_Enable_1_)
  N43: M3.pin_2, IC2.Out_2_(_Controlled_by_Enable_1_)
  N44: IC2.Out_3_(_Controlled_by_Enable_2_), M4.pin2
  N45: IC2.Out_4_(_Controlled_by_Enable_2_), M4.pin1
  N46: IC3.Out_1_(_Controlled_by_Enable_1_), M5.pin_1
  N47: IC3.Out_2_(_Controlled_by_Enable_1_), M5.pin_2
  N48: IC3.+Vmotor, U3.+

custom parts:
  linear actuator: Generic linear actuator.
